# Fritzing sketch LightSensor (saved by Fritzing 0.9.0b)
circuit board: 8.46667cm x 5.64444cm
breadboards: 1

parts:
  R1 = Photocell (LDR) [package=THT]
  Part1 = Arduino Nano (Rev3.0)
  R2 = Resistor [tolerance=±5% resistance=10k package=THT]

nets:
  N1: R1.pin_0, Part1.A0, R2.Pin_1
  N2: R1.pin_1, Part1.5V
  N3: Part1.GND, R2.Pin_0
  SCL: Part1.A5
  SDA: Part1.A4
